// Logisim project mct4.circ as structural Verilog: 2 circuits, main circuit main
module main (
  input  in_1
);

  wire and_1_out, and_2_out, apu_1_carry, clock_1_out, comparator_1_eq, or_1_out, Reset_out, Step_out,
       t_ff_1_q, ToggleClock_out;
  wire [1:0] Carry_q;
  wire [2:0] counter_1_q;
  wire [3:0] binary_to_bcd_converter_1_p2, binary_to_bcd_converter_1_p3, binary_to_bcd_converter_1_p4,
       controlled_buffer_1_out, MAR_q, PC_q;
  wire [7:0] A_q, apu_1_sum, B_q, IR_q, ram_1_dout, register_1_q, undriven;
  wire [7:4] controlled_buffer_1_out_2;
  wire [15:0] pla_1_out;

  RAM #(.addrWidth(4), .enables("line")) ram_1 (
    .addr(MAR_q), .we(pla_1_out[6]), .clk(or_1_out),
    .din({controlled_buffer_1_out_2, controlled_buffer_1_out}), .dout(ram_1_dout));
  Counter #(.max('h7), .width(3)) counter_1 (
    .clr(Reset_out), .load(pla_1_out[15]), .up(1'b1), .count(1'b1), .clk(or_1_out), .D(3'b000),
    .Q(counter_1_q));  // open: carry
  Register #(.width(4)) MAR (
    .D(controlled_buffer_1_out), .en(pla_1_out[8]), .clk(or_1_out), .Q(MAR_q), .clr(Reset_out));
  Register IR (
    .D({controlled_buffer_1_out_2, controlled_buffer_1_out}), .en(pla_1_out[4]), .clk(or_1_out), .Q(IR_q),
    .clr(Reset_out));
  LED led_1 (.in(t_ff_1_q));
  Button ToggleClock (.out(ToggleClock_out));
  Button Step (.out(Step_out));
  Button Reset (.out(Reset_out));
  assign {controlled_buffer_1_out_2, controlled_buffer_1_out} = pla_1_out[7] ? ram_1_dout : 8'bz;  // Controlled_Buffer controlled_buffer_1
  T_Flip_Flop t_ff_1 (.T(1'b1), .clk(ToggleClock_out), .Q(t_ff_1_q), .reset(pla_1_out[0]));  // open: Qn, preset
  assign {controlled_buffer_1_out_2, controlled_buffer_1_out} = pla_1_out[5] ? {4'b0000, IR_q[3:0]} : 8'bz;  // Controlled_Buffer controlled_buffer_2
  PLA #(.in_width(9), .out_width(16), .\table ("xxxxxx000 0000000100000100 # FETCH: PC to MAR\nxxxxxx001 0000000010011000 # FETCH: RAM to IR\n0000xx010 1000000000000000 # NOP\n0001xx010 1000001000100000 # LDI: IR to A\n0010xx010 0000000100100000 # LDA: IR to MAR\n0010xx011 1000001010000000 # LDA: RAM to A\n0011xx010 0000000100100000 # STA: IR to MAR\n0011xx011 1000010001000000 # STA: A to RAM\n0101xx010 0000000100100000 # ADD; IR to MAR\n0101xx011 0000100010000000 # ADD: RAM to B\n0101xx100 1001001000000000 # ADD: SUM to A\n0110xx010 0000000100100000 # SUB; IR to MAR\n0110xx011 0000100010000000 # SUB: RAM to B\n0110xx100 1011001000000000 # SUB: SUM to A\n0111xx010 1100010000000000 # OUT: A to OUT\n1000xx010 1000000000100010 # JMP: IR to PC\n10011x010 1000000000100010 # JZ: IR to PC\n10010x010 1000000000000000 # JZ: NOP\n1010x1010 1000000000100010 # JC: IR to PC\n1010x0010 1000000000000000 # JC: NOP\n1111xx010 0000000000000001 # HLT")) pla_1 (
    .in({IR_q[7:4], Carry_q, counter_1_q}), .out(pla_1_out));
  Clock clock_1 (.out(clock_1_out));
  and and_1 (and_1_out, clock_1_out, t_ff_1_q);
  or or_1 (or_1_out, Step_out, and_1_out);
  LedBar ledbar_1 (
    .led0(controlled_buffer_1_out_2[7]), .led1(controlled_buffer_1_out_2[6]),
    .led2(controlled_buffer_1_out_2[5]), .led3(controlled_buffer_1_out_2[4]),
    .led4(controlled_buffer_1_out[3]), .led5(controlled_buffer_1_out[2]), .led6(controlled_buffer_1_out[1]),
    .led7(controlled_buffer_1_out[0]));
  // DipSwitch dipswitch_1: pin names not known
  assign {controlled_buffer_1_out_2, controlled_buffer_1_out} = in_1 ? undriven : 8'bz;  // Controlled_Buffer controlled_buffer_3
  Register A (
    .D({controlled_buffer_1_out_2, controlled_buffer_1_out}), .en(pla_1_out[9]), .clk(or_1_out), .Q(A_q),
    .clr(Reset_out));
  Register B (
    .D({controlled_buffer_1_out_2, controlled_buffer_1_out}), .en(pla_1_out[11]), .clk(or_1_out), .Q(B_q),
    .clr(Reset_out));
  assign {controlled_buffer_1_out_2, controlled_buffer_1_out} = pla_1_out[10] ? A_q : 8'bz;  // Controlled_Buffer controlled_buffer_4
  assign {controlled_buffer_1_out_2, controlled_buffer_1_out} = pla_1_out[12] ? apu_1_sum : 8'bz;  // Controlled_Buffer controlled_buffer_5
  assign {controlled_buffer_1_out_2, controlled_buffer_1_out} = pla_1_out[2] ? {4'b0000, PC_q} : 8'bz;  // Controlled_Buffer controlled_buffer_6
  Counter #(.max('hf), .width(4)) PC (
    .clr(Reset_out), .load(pla_1_out[1]), .up(1'b1), .count(pla_1_out[3]), .clk(or_1_out),
    .D(controlled_buffer_1_out), .Q(PC_q));  // open: carry
  Register register_1 (
    .D({controlled_buffer_1_out_2, controlled_buffer_1_out}), .en(pla_1_out[14]), .clk(or_1_out),
    .Q(register_1_q), .clr(Reset_out));
  apu apu_1 (.A(A_q), .B(B_q), .AS(pla_1_out[13]), .sum(apu_1_sum), .carry(apu_1_carry));
  Hex_Digit_Display hex_digit_display_1 (.value(register_1_q[7:4]));  // open: dp
  Hex_Digit_Display hex_digit_display_2 (.value(binary_to_bcd_converter_1_p2));  // open: dp
  // Binary_to_BCD_converter #(.binvalue(8)) binary_to_bcd_converter_1: pin names not known; wires that end beside it: register_1_q, binary_to_bcd_converter_1_p2, binary_to_bcd_converter_1_p3, binary_to_bcd_converter_1_p4
  D_Flip_Flop Carry (.D(apu_1_carry), .clk(and_2_out), .Q(Carry_q[0]), .reset(Reset_out));  // open: Qn, preset
  D_Flip_Flop Zero (.D(comparator_1_eq), .clk(and_2_out), .Q(Carry_q[1]), .reset(Reset_out));  // open: Qn, preset
  Comparator comparator_1 (.a(apu_1_sum), .b({8{1'b0}}), .eq(comparator_1_eq));  // open: gt, lt
  and and_2 (and_2_out, or_1_out, pla_1_out[12]);
  Hex_Digit_Display hex_digit_display_3 (.value(register_1_q[3:0]));  // open: dp
  Hex_Digit_Display hex_digit_display_4 (.value(binary_to_bcd_converter_1_p3));  // open: dp
  Hex_Digit_Display hex_digit_display_5 (.value(binary_to_bcd_converter_1_p4));  // open: dp
endmodule

module apu (
  input  [7:0] A,
  input  [7:0] B,
  input  AS,
  output [7:0] sum,
  output carry
);

  wire adder_1_cout, subtractor_1_bout;
  wire [7:0] adder_1_out, subtractor_1_out;

  Adder adder_1 (.a(A), .b(B), .out(adder_1_out), .cout(adder_1_cout));  // open: cin
  Subtractor subtractor_1 (.a(A), .b(B), .out(subtractor_1_out), .bout(subtractor_1_bout));  // open: bin
  Multiplexer #(.width(8)) multiplexer_1 (.in0(adder_1_out), .in1(subtractor_1_out), .out(sum), .sel(AS));
  Multiplexer multiplexer_2 (.in0(adder_1_cout), .in1(subtractor_1_bout), .out(carry), .sel(AS));
endmodule
